// Logisim project Artifical_Neuron.circ as structural Verilog: 5 circuits, main circuit main
module main (
  output [2:0] out_1,
  output [2:0] out_2,
  output [3:0] out_3,
  output [2:0] out_4
);

  wire and_1_out, bit_pattern_recognition_1_output, clock_1_out, clock_2_out, combinational_logic_1_green,
       combinational_logic_1_red, combinational_logic_1_yellow, decoder_1_out0, decoder_1_out1,
       decoder_1_out2, decoder_1_out3, decoder_1_out4, decoder_1_out5, decoder_1_out6, decoder_1_out7,
       j_k_ff_1_qn, j_k_ff_2_qn, or_1_out, or_2_out, or_3_out, Primary_Clock_out, Secondary_Clock_out,
       shift_register_1_out, shift_register_2_q0, shift_register_2_q1, shift_register_2_q2,
       shift_register_2_q3;
  wire [2:0] activation_function_1_output, counter_1_output;
  wire [3:0] bitadder_2_out;
  wire [7:0] Input_out, random_1_out;

  Clock #(.highDuration(2), .lowDuration(4)) clock_1 (.out(clock_1_out));
  Random random_1 (.clk(clock_1_out), .next(1'b1), .out(random_1_out));  // open: clr
  Clock Secondary_Clock (.out(Secondary_Clock_out));
  Clock #(.highDuration(2), .lowDuration(4)) Primary_Clock (.out(Primary_Clock_out));
  BitAdder #(.width(1)) bitadder_1 (
    .in0(random_1_out[0]), .in1(random_1_out[1]), .in2(random_1_out[2]), .in3(random_1_out[3]),
    .in4(random_1_out[4]), .in5(random_1_out[5]), .in6(random_1_out[6]), .in7(random_1_out[7]),
    .out({out_3[3], out_2}));
  Random Input (.clk(Primary_Clock_out), .next(1'b1), .out(Input_out));  // open: clr
  Multiplexer #(.select(3), .width(3), .enable("false")) multiplexer_1 (
    .in0(3'b111), .in1(3'b111), .in2(out_2), .in3(out_2), .in4(out_2), .in5(out_2), .in6(3'b111),
    .in7(3'b111), .out(out_1), .sel(out_2));
  Clock clock_2 (.out(clock_2_out));
  BitAdder #(.width(1)) bitadder_2 (
    .in0(Input_out[0]), .in1(Input_out[1]), .in2(Input_out[2]), .in3(Input_out[3]), .in4(Input_out[4]),
    .in5(Input_out[5]), .in6(Input_out[6]), .in7(Input_out[7]), .out(bitadder_2_out));
  Shift_Register #(.length(3)) shift_register_1 (
    .clk(clock_2_out), .out(shift_register_1_out), .load(clock_1_out), .d0(out_1[2]), .d1(out_1[1]),
    .d2(out_1[0]));  // open: shift, in, clr, q0, q1, q2
  Activation_Function activation_function_1 (.Output(activation_function_1_output), .Input(bitadder_2_out));
  Shift_Register #(.length(4)) shift_register_2 (
    .in(shift_register_1_out), .clk(clock_2_out), .q0(shift_register_2_q0), .q1(shift_register_2_q1),
    .q2(shift_register_2_q2), .q3(shift_register_2_q3));  // open: shift, out, load, clr, d0, d1, d2, d3
  and and_1 (and_1_out, ~shift_register_2_q3, shift_register_2_q2, ~shift_register_2_q1, shift_register_2_q0);  // AND_Gate
  Counter counter_1 (.Input(bit_pattern_recognition_1_output), .Output(counter_1_output));
  Bit_Pattern_Recognition bit_pattern_recognition_1 (
    .Secondary_Clock(Secondary_Clock_out), .Input(activation_function_1_output),
    .Output(bit_pattern_recognition_1_output), .Primary_Clock(Primary_Clock_out));
  J_K_Flip_Flop j_k_ff_1 (
    .J(and_1_out), .clk(and_1_out), .K(and_1_out), .Q(out_4[0]), .Qn(j_k_ff_1_qn), .preset(1'b0), .en(1'b1),
    .reset(1'b0));
  Decoder #(.select(3), .enable("false")) decoder_1 (
    .out0(decoder_1_out0), .out1(decoder_1_out1), .out2(decoder_1_out2), .out3(decoder_1_out3),
    .out4(decoder_1_out4), .out5(decoder_1_out5), .out6(decoder_1_out6), .out7(decoder_1_out7), .sel(out_4));
  Combinational_Logic combinational_logic_1 (
    .Green(combinational_logic_1_green), .Yellow(combinational_logic_1_yellow),
    .Red(combinational_logic_1_red), .Input(counter_1_output));
  J_K_Flip_Flop j_k_ff_2 (
    .J(and_1_out), .clk(j_k_ff_1_qn), .K(and_1_out), .Q(out_4[1]), .Qn(j_k_ff_2_qn), .preset(1'b0),
    .en(1'b1), .reset(1'b0));
  LED led_1 (.in(combinational_logic_1_green));
  LED led_2 (.in(combinational_logic_1_yellow));
  LED led_3 (.in(combinational_logic_1_red));
  or or_1 (or_1_out, decoder_1_out0, decoder_1_out1, decoder_1_out2);
  or or_2 (or_2_out, decoder_1_out3, decoder_1_out4, decoder_1_out5);
  or or_3 (or_3_out, decoder_1_out5, decoder_1_out6, decoder_1_out7);
  J_K_Flip_Flop j_k_ff_3 (
    .J(and_1_out), .clk(j_k_ff_2_qn), .K(and_1_out), .Q(out_4[2]), .preset(1'b0), .en(1'b1), .reset(1'b0));  // open: Qn
  LED led_4 (.in(or_1_out));
  LED led_5 (.in(or_2_out));
  LED led_6 (.in(or_3_out));

  assign out_3[2:0] = out_2;

  // Notes on the sheet:
  //   Design Project EEE
  //   Group 19
  //   Block Diagram
  //   Original Circuit Diagram
endmodule

// Activation
module Activation_Function (
  input  [3:0] Input,
  output [2:0] Output
);

  Multiplexer #(.select(3), .width(3), .enable("false")) multiplexer_1 (
    .in0(3'b111), .in1(3'b111), .in2(Input[2:0]), .in3(Input[2:0]), .in4(Input[2:0]), .in5(Input[2:0]),
    .in6(3'b111), .in7(3'b111), .out(Output), .sel(Input[2:0]));
endmodule

// Pattern
module Bit_Pattern_Recognition (
  input  [2:0] Input,
  input  Primary_Clock,
  input  Secondary_Clock,
  output Output
);

  wire not_1_out, not_2_out, shift_register_1_out, shift_register_2_q0, shift_register_2_q1,
       shift_register_2_q2, shift_register_2_q3;

  Shift_Register #(.length(3)) shift_register_1 (
    .clk(Secondary_Clock), .out(shift_register_1_out), .load(Primary_Clock), .d0(Input[2]), .d1(Input[1]),
    .d2(Input[0]));  // open: shift, in, clr, q0, q1, q2
  Shift_Register #(.length(4)) shift_register_2 (
    .in(shift_register_1_out), .clk(Secondary_Clock), .q0(shift_register_2_q0), .q1(shift_register_2_q1),
    .q2(shift_register_2_q2), .q3(shift_register_2_q3));  // open: shift, out, load, clr, d0, d1, d2, d3
  not not_1 (not_1_out, shift_register_2_q3);
  and and_1 (Output, not_1_out, shift_register_2_q2, not_2_out, shift_register_2_q0);
  not not_2 (not_2_out, shift_register_2_q1);
endmodule

module Counter (
  input  Input,
  output [2:0] Output
);

  wire j_k_ff_1_qn, j_k_ff_2_qn;

  J_K_Flip_Flop j_k_ff_1 (
    .J(Input), .clk(Input), .K(Input), .Q(Output[0]), .Qn(j_k_ff_1_qn), .preset(1'b0), .en(1'b1), .reset(1'b0));
  J_K_Flip_Flop j_k_ff_2 (
    .J(Input), .clk(j_k_ff_1_qn), .K(Input), .Q(Output[1]), .Qn(j_k_ff_2_qn), .preset(1'b0), .en(1'b1),
    .reset(1'b0));
  J_K_Flip_Flop j_k_ff_3 (
    .J(Input), .clk(j_k_ff_2_qn), .K(Input), .Q(Output[2]), .preset(1'b0), .en(1'b1), .reset(1'b0));  // open: Qn
endmodule

// Combinational
module Combinational_Logic (
  input  [2:0] Input,
  output Green,
  output Yellow,
  output Red
);

  wire decoder_1_out0, decoder_1_out1, decoder_1_out2, decoder_1_out3, decoder_1_out4, decoder_1_out5,
       decoder_1_out6, decoder_1_out7;

  Decoder #(.select(3), .enable("false")) decoder_1 (
    .out0(decoder_1_out0), .out1(decoder_1_out1), .out2(decoder_1_out2), .out3(decoder_1_out3),
    .out4(decoder_1_out4), .out5(decoder_1_out5), .out6(decoder_1_out6), .out7(decoder_1_out7), .sel(Input));
  or or_1 (Green, decoder_1_out0, decoder_1_out1, decoder_1_out2);
  or or_2 (Yellow, decoder_1_out3, decoder_1_out4, decoder_1_out5);
  or or_3 (Red, decoder_1_out5, decoder_1_out6, decoder_1_out7);
endmodule
